// Logisim project display20s.circ as structural Verilog: 2 circuits, main circuit main
module main (
  input  A,
  input  B,
  input  C,
  input  D
);

  wire display20s_1_a_2, display20s_1_b_2, display20s_1_c_2, display20s_1_d_2, display20s_1_e,
       display20s_1_f, display20s_1_g, display20s_1_h, display20s_1_i, display20s_1_j, display20s_1_k,
       display20s_1_l, display20s_1_m, display20s_1_n, display20s_1_o, display20s_1_p, display20s_1_q,
       display20s_1_r, display20s_1_s, display20s_1_t;

  Display20S display20s_1 (
    .A(A), .B(B), .C(C), .D(D), .a_2(display20s_1_a_2), .b_2(display20s_1_b_2), .c_2(display20s_1_c_2),
    .d_2(display20s_1_d_2), .e(display20s_1_e), .f(display20s_1_f), .g(display20s_1_g), .h(display20s_1_h),
    .i(display20s_1_i), .j(display20s_1_j), .k(display20s_1_k), .l(display20s_1_l), .m(display20s_1_m),
    .n(display20s_1_n), .o(display20s_1_o), .p(display20s_1_p), .q(display20s_1_q), .r(display20s_1_r),
    .s(display20s_1_s), .t(display20s_1_t));
  LED led_1 (.in(display20s_1_a_2));
  LED led_2 (.in(display20s_1_e));
  LED led_3 (.in(display20s_1_i));
  LED led_4 (.in(display20s_1_m));
  LED led_5 (.in(display20s_1_q));
  LED led_6 (.in(display20s_1_c_2));
  LED led_7 (.in(display20s_1_b_2));
  LED led_8 (.in(display20s_1_g));
  LED led_9 (.in(display20s_1_f));
  LED led_10 (.in(display20s_1_k));
  LED led_11 (.in(display20s_1_j));
  LED led_12 (.in(display20s_1_n));
  LED led_13 (.in(display20s_1_o));
  LED led_14 (.in(display20s_1_r));
  LED led_15 (.in(display20s_1_s));
  LED led_16 (.in(display20s_1_d_2));
  LED led_17 (.in(display20s_1_h));
  LED led_18 (.in(display20s_1_l));
  LED led_19 (.in(display20s_1_p));
  LED led_20 (.in(display20s_1_t));

  // Notes on the sheet:
  //   0000
  //   0001
  //   0010
  //   0011
  //   0100
  //   0101
  //   0110
  //   0111
  //   1000
  //   1001
  //   1010
  //   1011
  //   1100
  //   1101
  //   1110
  //   1111
  //   0
  //   1
  //   2
  //   3
  //   4
  //   5
  //   6
  //   7
  //   8
  //   9
  //   A
  //   B
  //   C
  //   D
  //   E
  //   F
endmodule

module Display20S (
  input  A,
  input  B,
  input  C,
  input  D,
  output a_2,
  output b_2,
  output c_2,
  output d_2,
  output e,
  output f,
  output g,
  output h,
  output i,
  output j,
  output k,
  output l,
  output m,
  output n,
  output o,
  output p,
  output q,
  output r,
  output s,
  output t
);

  wire and_1_out, and_2_out, and_3_out, and_4_out, and_5_out, and_6_out, and_7_out, and_8_out, and_9_out,
       and_10_out, and_11_out, and_12_out, and_13_out, and_14_out, and_15_out, and_16_out, and_17_out,
       and_18_out, and_19_out, and_20_out, and_21_out, and_22_out, and_23_out, and_24_out, and_25_out,
       and_26_out, and_27_out, and_28_out, and_29_out, and_30_out, and_31_out, and_32_out, and_33_out,
       and_34_out, and_35_out, and_36_out, and_37_out, and_38_out, and_39_out, and_40_out, and_41_out,
       and_42_out, and_43_out, and_44_out, and_45_out, and_47_out, and_48_out, and_49_out, and_50_out,
       and_51_out, and_52_out, and_53_out, and_54_out, and_55_out, and_56_out, and_57_out, and_58_out,
       and_59_out, and_60_out, and_61_out, and_62_out, and_63_out, and_64_out, and_65_out, and_66_out,
       and_67_out, and_68_out, not_1_out, not_2_out, not_3_out, not_4_out, not_5_out, not_6_out, not_7_out,
       not_8_out, not_9_out, not_10_out, not_11_out, not_12_out, not_13_out, not_14_out, not_15_out,
       not_16_out, not_17_out, not_18_out, not_19_out, not_20_out, not_21_out, not_22_out, not_23_out,
       not_24_out, not_25_out, not_26_out, not_27_out, not_28_out, not_29_out, not_30_out, not_31_out,
       not_32_out, not_33_out, not_34_out, not_35_out, not_36_out, not_37_out, not_38_out, not_39_out,
       not_40_out, not_41_out, not_42_out, not_43_out, not_44_out, not_45_out, not_46_out, not_47_out,
       not_48_out, not_49_out, not_50_out, not_51_out, not_52_out, not_53_out, not_54_out, not_55_out,
       not_56_out, not_57_out, not_58_out, not_59_out, not_60_out, not_61_out, not_62_out, not_63_out,
       not_64_out, not_65_out, not_66_out, not_67_out, not_68_out, not_69_out, not_70_out, not_71_out,
       not_72_out, not_73_out, not_74_out, not_75_out, not_76_out, not_77_out, not_78_out, not_79_out,
       not_80_out, not_81_out, not_82_out, not_83_out, not_84_out, not_85_out, not_86_out, not_87_out;

  not not_1 (not_1_out, C);
  not not_2 (not_2_out, D);
  not not_3 (not_3_out, D);
  not not_4 (not_4_out, A);
  not not_5 (not_5_out, B);
  not not_6 (not_6_out, D);
  not not_7 (not_7_out, A);
  not not_8 (not_8_out, C);
  not not_9 (not_9_out, D);
  not not_10 (not_10_out, A);
  not not_11 (not_11_out, A);
  not not_12 (not_12_out, B);
  not not_13 (not_13_out, C);
  not not_14 (not_14_out, A);
  not not_15 (not_15_out, C);
  not not_16 (not_16_out, D);
  not not_17 (not_17_out, C);
  not not_18 (not_18_out, D);
  not not_19 (not_19_out, B);
  not not_20 (not_20_out, A);
  not not_21 (not_21_out, D);
  not not_22 (not_22_out, C);
  not not_23 (not_23_out, B);
  not not_24 (not_24_out, A);
  not not_25 (not_25_out, B);
  not not_26 (not_26_out, A);
  not not_27 (not_27_out, B);
  not not_28 (not_28_out, B);
  not not_29 (not_29_out, C);
  not not_30 (not_30_out, D);
  not not_31 (not_31_out, C);
  not not_32 (not_32_out, A);
  not not_33 (not_33_out, B);
  not not_34 (not_34_out, B);
  not not_35 (not_35_out, C);
  not not_36 (not_36_out, D);
  not not_37 (not_37_out, C);
  not not_38 (not_38_out, A);
  not not_39 (not_39_out, B);
  not not_40 (not_40_out, C);
  not not_41 (not_41_out, B);
  not not_42 (not_42_out, D);
  not not_43 (not_43_out, A);
  not not_44 (not_44_out, C);
  not not_45 (not_45_out, D);
  not not_46 (not_46_out, D);
  and and_1 (and_1_out, C, D);
  and and_2 (and_2_out, B, D);
  and and_3 (and_3_out, A, B);
  not not_47 (not_47_out, B);
  not not_48 (not_48_out, D);
  not not_49 (not_49_out, A);
  not not_50 (not_50_out, C);
  not not_51 (not_51_out, A);
  not not_52 (not_52_out, B);
  not not_53 (not_53_out, D);
  not not_54 (not_54_out, A);
  not not_55 (not_55_out, B);
  not not_56 (not_56_out, C);
  not not_57 (not_57_out, A);
  not not_58 (not_58_out, C);
  not not_59 (not_59_out, D);
  not not_60 (not_60_out, A);
  not not_61 (not_61_out, B);
  not not_62 (not_62_out, C);
  not not_63 (not_63_out, C);
  not not_64 (not_64_out, D);
  not not_65 (not_65_out, B);
  not not_66 (not_66_out, A);
  not not_67 (not_67_out, C);
  not not_68 (not_68_out, A);
  not not_69 (not_69_out, C);
  not not_70 (not_70_out, D);
  not not_71 (not_71_out, B);
  not not_72 (not_72_out, C);
  not not_73 (not_73_out, D);
  not not_74 (not_74_out, B);
  not not_75 (not_75_out, A);
  not not_76 (not_76_out, C);
  not not_77 (not_77_out, D);
  not not_78 (not_78_out, B);
  not not_79 (not_79_out, A);
  not not_80 (not_80_out, B);
  not not_81 (not_81_out, A);
  not not_82 (not_82_out, C);
  not not_83 (not_83_out, D);
  not not_84 (not_84_out, A);
  not not_85 (not_85_out, D);
  not not_86 (not_86_out, C);
  not not_87 (not_87_out, D);
  and and_4 (and_4_out, not_1_out, not_2_out);
  and and_5 (and_5_out, B, not_3_out);
  and and_6 (and_6_out, A, C);
  and and_7 (and_7_out, A, B);
  and and_8 (and_8_out, not_4_out, not_5_out, C, not_6_out);
  and and_9 (and_9_out, not_7_out, B, not_8_out, not_9_out);
  and and_10 (and_10_out, not_10_out, B, C, D);
  and and_11 (and_11_out, not_11_out, not_12_out, not_13_out, D);
  and and_12 (and_12_out, not_14_out, B, not_15_out, not_16_out);
  and and_13 (and_13_out, not_17_out, not_18_out);
  and and_14 (and_14_out, not_19_out, C, D);
  and and_15 (and_15_out, not_20_out, B, not_21_out);
  and and_16 (and_16_out, B, not_22_out);
  and and_17 (and_17_out, A, not_23_out);
  and and_18 (and_18_out, not_24_out, D);
  and and_19 (and_19_out, not_25_out, C);
  and and_20 (and_20_out, B, D);
  and and_21 (and_21_out, A, C);
  and and_22 (and_22_out, not_26_out, not_27_out);
  and and_23 (and_23_out, not_28_out, D);
  and and_24 (and_24_out, not_29_out, D);
  and and_25 (and_25_out, B, C, not_30_out);
  and and_26 (and_26_out, A, not_31_out);
  and and_27 (and_27_out, not_32_out, not_33_out);
  and and_28 (and_28_out, not_34_out, D);
  and and_29 (and_29_out, not_35_out, D);
  and and_30 (and_30_out, B, C, not_36_out);
  and and_31 (and_31_out, A, not_37_out);
  and and_32 (and_32_out, not_38_out, not_39_out, not_40_out, D);
  and and_33 (and_33_out, not_41_out, C, not_42_out);
  and and_34 (and_34_out, not_43_out, B, not_44_out, not_45_out);
  and and_35 (and_35_out, A, C, not_46_out);
  or or_1 (a_2, and_1_out, and_2_out, and_3_out);
  and and_36 (and_36_out, not_47_out, not_48_out);
  and and_37 (and_37_out, B, D);
  and and_38 (and_38_out, not_49_out, B, not_50_out);
  and and_39 (and_39_out, not_51_out, B, D);
  and and_40 (and_40_out, A, B, C);
  and and_41 (and_41_out, not_52_out, not_53_out);
  and and_42 (and_42_out, B, D);
  and and_43 (and_43_out, B, C);
  and and_44 (and_44_out, not_54_out, not_55_out, not_56_out, D);
  and and_45 (and_45_out, not_57_out, B, not_58_out, not_59_out);
  and and_46 (g, not_60_out, not_61_out, not_62_out, D);
  and and_47 (and_47_out, not_63_out, not_64_out);
  and and_48 (and_48_out, not_65_out, C);
  and and_49 (and_49_out, not_66_out, C, D);
  and and_50 (and_50_out, A, not_67_out);
  and and_51 (and_51_out, not_68_out, not_69_out, not_70_out);
  and and_52 (and_52_out, not_71_out, C, D);
  and and_53 (and_53_out, B, not_72_out);
  and and_54 (and_54_out, B, not_73_out);
  and and_55 (and_55_out, A, D);
  and and_56 (and_56_out, A, C);
  and and_57 (and_57_out, not_74_out, C, D);
  and and_58 (and_58_out, not_75_out, B, not_76_out, D);
  and and_59 (and_59_out, B, C, not_77_out);
  and and_60 (and_60_out, A, not_78_out);
  and and_61 (and_61_out, A, C);
  and and_62 (and_62_out, not_79_out, D);
  and and_63 (and_63_out, A, not_80_out);
  and and_64 (and_64_out, not_81_out, not_82_out, not_83_out);
  and and_65 (and_65_out, not_84_out, B, not_85_out);
  and and_66 (and_66_out, A, not_86_out, D);
  and and_67 (and_67_out, A, C, not_87_out);
  and and_68 (and_68_out, A, B, C);
  or or_2 (m, and_4_out, and_5_out, and_6_out, and_7_out);
  or or_3 (n, and_8_out, and_9_out, and_10_out);
  or or_4 (o, and_11_out, and_12_out);
  or or_5 (p, and_13_out, and_14_out, and_15_out, and_16_out, and_17_out);
  or or_6 (q, and_18_out, and_19_out, and_20_out, and_21_out);
  or or_7 (r, and_22_out, and_23_out, and_24_out, and_25_out, and_26_out);
  or or_8 (s, and_27_out, and_28_out, and_29_out, and_30_out, and_31_out);
  or or_9 (t, and_32_out, and_33_out, and_34_out, and_35_out);
  or or_10 (b_2, and_36_out, C, and_37_out, A);
  or or_11 (d_2, and_38_out, and_39_out, and_40_out);
  or or_12 (e, and_41_out, and_42_out, and_43_out, A);
  or or_13 (f, and_44_out, and_45_out);
  or or_14 (h, and_47_out, and_48_out, and_49_out, and_50_out);
  or or_15 (i, and_51_out, and_52_out, and_53_out, and_54_out, and_55_out, and_56_out);
  or or_16 (j, and_57_out, and_58_out, and_59_out, and_60_out, and_61_out);
  or or_17 (k, and_62_out, C, and_63_out);
  or or_18 (l, and_64_out, and_65_out, and_66_out, and_67_out, and_68_out);

  assign c_2 = 1'b1;
endmodule
